// Logisim project op_cde.circ as structural Verilog: 1 circuit, main circuit opcode
module opcode (
  input  [7:0] data_input,
  input  cargaRI,
  input  clock,
  input  reset,
  output [3:0] flag_out
);

  wire [3:0] register_1_q;

  Register register_1 (.D(data_input), .en(cargaRI), .clk(clock), .Q({flag_out, register_1_q}), .clr(reset));
endmodule
